# Fritzing sketch diagrama_catodo (saved by Fritzing 0.9.3b)
breadboards: 1

parts:
  R1 = Resistor [tolerance=±5% resistance=220 package=THT]
  Componente1 = Arduino Uno (Rev3) - ICSP
  R2 = Resistor [tolerance=±5% resistance=220 package=THT]
  R3 = Resistor [tolerance=±5% resistance=220 package=THT]
  LED1 = RGB LED - (4 legs) [package="5 mm [THT]"]  # not connected

nets:
  N1: R1.Pin_0, Componente1.D11_PWM/MOSI
  N2: Componente1.D9_PWM, R3.Pin_0
  N3: Componente1.D10_PWM/SS, R2.Pin_0
